// Logisim project CPU.circ as structural Verilog: 2 circuits, main circuit main
module main (
  input  [7:0] in_1,
  input  in_2,
  input  in_3,
  input  in_4,
  input  in_5,
  output [7:0] out_6
);

  Gen_Reg gen_reg_1 (.d_bus(in_1), .OE(in_2), .load(in_3), .clk(in_4), .clear(in_5), .d_out(out_6));
endmodule

module Gen_Reg (
  input  [7:0] d_bus,
  input  OE,
  input  load,
  input  clk,
  input  clear,
  output [7:0] d_out
);

  wire [7:0] register_1_q;

  Register register_1 (.D(d_bus), .en(load), .clk(clk), .Q(register_1_q), .clr(clear));
  assign d_out = OE ? register_1_q : 8'bz;  // Controlled_Buffer controlled_buffer_1
endmodule
